// Logisim project 25CSB1A74_ROHITKUMARGUPTA_COA.circ as structural Verilog
module main (
  output [15:0] pc,
  output [15:0] r0,
  output [15:0] r1,
  output [15:0] r2,
  output [15:0] r3,
  output [15:0] r4,
  output [15:0] r5,
  output [15:0] r6,
  output [15:0] r7,
  output [15:0] r8,
  output [15:0] r9,
  output [15:0] r10,
  output [15:0] r11,
  output [15:0] r12,
  output [15:0] r13,
  output [15:0] r14,
  output [15:0] r15,
  output halt
);

  wire and_1_out, and_2_out, bit_extender_2_out, clock_1_out, control_unit_1_p5, control_unit_1_p6,
       control_unit_1_p7, control_unit_1_p8, control_unit_1_p9, control_unit_1_p10, control_unit_1_p11,
       control_unit_1_p12, control_unit_1_p13, control_unit_1_p15, control_unit_1_p16, control_unit_1_p17,
       control_unit_1_p18, control_unit_1_p19, control_unit_1_p20, control_unit_1_p21, n16_bit_alu_1_p5,
       or_1_out, or_2_out, reset_out;
  wire [1:0] control_unit_1_p14;
  wire [3:0] control_unit_1_p2, control_unit_1_p3, control_unit_1_p4, multiplexer_2_out, multiplexer_3_out,
       multiplexer_4_out;
  wire [15:0] bit_extender_1_out, control_unit_1_p1, immediate_unit_1_p8, multiplexer_1_out,
       multiplexer_5_out, multiplexer_6_out, multiplexer_7_out, n16_bit_alu_1_p4, program_counter_1_pc_1,
       ram_2_data, register_file_1_s, register_file_1_t;

  Halt halt_1 (.instruction(control_unit_1_p1), .clock(clock_1_out), .reset(reset_out), .HALT(or_1_out), .halt_2(halt));
  Clock clock_1 (.out(clock_1_out));
  or or_1 (or_1_out, n16_bit_alu_1_p5, control_unit_1_p17);
  Button reset (.out(reset_out));
  or or_2 (or_2_out, control_unit_1_p10, control_unit_1_p7, control_unit_1_p5);
  Multiplexer #(.width(16), .enable("false")) multiplexer_1 (
    .in0(immediate_unit_1_p8), .in1(multiplexer_7_out), .out(multiplexer_1_out), .sel(control_unit_1_p7));
  program_counter program_counter_1 (
    .C(and_1_out), .BRANCH_VALUE(multiplexer_1_out), .INSTRUCTION_ADRRESS(pc), .RESET(reset_out),
    .BRANCH_RELATIVE(and_2_out), .BRANCH_ABSOLUTE(or_2_out), .PC_1(program_counter_1_pc_1));
  and and_1 (and_1_out, ~halt, clock_1_out);  // AND_Gate
  // resources_control_unit control_unit_1: pin names not known; wires that end beside it: control_unit_1_p1, control_unit_1_p2, control_unit_1_p3, control_unit_1_p4, control_unit_1_p5, control_unit_1_p6, control_unit_1_p7, control_unit_1_p8, control_unit_1_p9, control_unit_1_p10, control_unit_1_p11, control_unit_1_p12, control_unit_1_p13, control_unit_1_p14, control_unit_1_p15, control_unit_1_p16, control_unit_1_p17, control_unit_1_p18, control_unit_1_p19, control_unit_1_p20, control_unit_1_p21
  RAM #(.addrWidth(16), .dataWidth(16)) ram_1 (
    .addr(pc), .data(control_unit_1_p1), .clk(and_1_out), .ld(1'b1), .clr(reset_out));  // open: sel
  Multiplexer #(.width(4), .enable("false")) multiplexer_2 (
    .in0(control_unit_1_p3), .in1(4'b0000), .out(multiplexer_2_out), .sel(control_unit_1_p21));
  Multiplexer #(.width(4), .enable("false")) multiplexer_3 (
    .in0(control_unit_1_p2), .in1(control_unit_1_p4), .out(multiplexer_3_out), .sel(control_unit_1_p6));
  Multiplexer #(.width(4), .enable("false")) multiplexer_4 (
    .in0(control_unit_1_p4), .in1(control_unit_1_p2), .out(multiplexer_4_out), .sel(control_unit_1_p8));
  assign bit_extender_1_out = {{12{1'b0}}, control_unit_1_p2};  // Bit_Extender bit_extender_1
  register_file register_file_1 (
    .DATA(multiplexer_7_out), .rd(multiplexer_4_out), .rt(multiplexer_3_out), .rs(multiplexer_2_out),
    .r0(r0), .r1(r1), .r2(r2), .r3(r3), .r4(r4), .r5(r5), .r6(r6), .r7(r7), .r8(r8), .r9(r9), .r10(r10),
    .r11(r11), .r12(r12), .r13(r13), .r14(r14), .r15(r15), .T(register_file_1_t), .S(register_file_1_s),
    .WRITE(control_unit_1_p9), .C(and_1_out), .RESET(reset_out));
  // immediate_unit immediate_unit_1: pin names not known; wires that end beside it: control_unit_1_p11, control_unit_1_p12, control_unit_1_p13, control_unit_1_p5, control_unit_1_p7, control_unit_1_p10, control_unit_1_p1, immediate_unit_1_p8
  Multiplexer #(.width(16), .enable("false")) multiplexer_5 (
    .in0(register_file_1_s), .in1(immediate_unit_1_p8), .out(multiplexer_5_out), .sel(control_unit_1_p18));
  Multiplexer #(.width(16), .enable("false")) multiplexer_6 (
    .in0(register_file_1_t), .in1(bit_extender_1_out), .out(multiplexer_6_out), .sel(control_unit_1_p20));
  // _16_bit_ALU 16_bit_alu_1: pin names not known; wires that end beside it: multiplexer_5_out, multiplexer_6_out, control_unit_1_p19, n16_bit_alu_1_p4, n16_bit_alu_1_p5
  and and_2 (and_2_out, control_unit_1_p13, bit_extender_2_out);
  Bit_Extender #(.in_width(16), .out_width(1)) bit_extender_2 (.in(n16_bit_alu_1_p4), .out(bit_extender_2_out));
  RAM #(.addrWidth(16), .dataWidth(16), .bus("separate")) ram_2 (
    .addr(n16_bit_alu_1_p4), .din(register_file_1_t), .data(ram_2_data), .str(control_unit_1_p16),
    .clk(and_1_out), .ld(control_unit_1_p15), .clr(reset_out));  // open: sel
  Multiplexer #(.select(2), .width(16), .enable("false")) multiplexer_7 (
    .in0(n16_bit_alu_1_p4), .in1(ram_2_data), .in2(immediate_unit_1_p8), .in3(program_counter_1_pc_1),
    .out(multiplexer_7_out), .sel(control_unit_1_p14));

  // Notes on the sheet:
  //   current instruction
  //   reset button
  //   clock signal
  //   overflow
  //   unknown instruction
  //   instruction memory
  //   rs
  //   rt
  //   rd
  //   write data
  //   DATA
  //   S
  //   T
  //   clock signal
  //   reset
  //   ALU op code
  //   immediate / signed
  //   data memory
  //   program counter + 1
  //   MemToReg
  //   write data
endmodule

module Halt (
  input  [15:0] instruction,
  input  HALT,
  input  clock,
  input  reset,
  output halt_2
);

  wire and_1_out, comparator_1_eq, comparator_2_gt, counter_1_carry, or_1_out, or_2_out, register_1_q;
  wire [11:0] counter_1_q;

  Comparator #(.width(16), .mode("unsigned")) comparator_1 (
    .a(instruction), .b({16{1'b0}}), .eq(comparator_1_eq));  // open: gt, lt
  Counter #(.width(12), .max('hfff), .trigger("falling")) counter_1 (
    .Q(counter_1_q), .carry(counter_1_carry), .clk(clock), .clr(reset));  // open: load, D, count
  or or_1 (or_1_out, comparator_1_eq, counter_1_carry);
  Comparator #(.width(12), .mode("unsigned")) comparator_2 (
    .a(counter_1_q), .b({12{1'b0}}), .gt(comparator_2_gt));  // open: eq, lt
  or or_2 (or_2_out, register_1_q, and_1_out);
  and and_1 (and_1_out, or_1_out, comparator_2_gt);
  Register #(.width(1)) register_1 (.D(or_2_out), .Q(register_1_q), .clk(clock), .clr(reset));  // open: en
  or or_3 (halt_2, register_1_q, HALT);

  // Notes on the sheet:
  //   halt becomes and stays asserted if the instruction is 0000 (not in the first clock cycle) or the end of the counter is reached (2^12)
endmodule

module program_counter (
  input  BRANCH_ABSOLUTE,
  input  C,
  input  [15:0] BRANCH_VALUE,
  input  BRANCH_RELATIVE,
  input  RESET,
  output [15:0] PC_1,
  output [15:0] INSTRUCTION_ADRRESS
);

  wire [15:0] add_2_p3, multiplexer_1_out, n16_bit_register_1_p2;

  // project1_16_bit_register 16_bit_register_1: pin names not known; wires that end beside it: C, n16_bit_register_1_p2, 1'b1, RESET, INSTRUCTION_ADRRESS
  // add add_1: pin names not known; wires that end beside it: 16'h1, INSTRUCTION_ADRRESS, PC_1
  // add add_2: pin names not known; wires that end beside it: PC_1, BRANCH_VALUE, add_2_p3
  Multiplexer #(.width(16), .enable("false")) multiplexer_1 (
    .in0(PC_1), .in1(add_2_p3), .out(multiplexer_1_out), .sel(BRANCH_RELATIVE));
  Multiplexer #(.width(16), .enable("false")) multiplexer_2 (
    .in0(multiplexer_1_out), .in1(BRANCH_VALUE), .out(n16_bit_register_1_p2), .sel(BRANCH_ABSOLUTE));

  // Notes on the sheet:
  //   WRITE ENABLE
  //   new pc value or branch address
  //   PC + 1 / (+4)
  //   target address is calculated on the current PC if 1
  //   absolute branch will jump to specified address regardless the current PC if 1
endmodule

module _16_bit_register (
  input  C,
  input  [15:0] INPUT,
  input  RESET,
  input  WRITE,
  output [15:0] Q
);

  D_Flip_Flop #(.trigger("falling")) d_ff_1 (
    .clk(C), .D(INPUT[0]), .Q(Q[0]), .en(WRITE), .reset(RESET));  // open: Qn, preset
  D_Flip_Flop #(.trigger("falling")) d_ff_2 (
    .clk(C), .D(INPUT[1]), .Q(Q[1]), .en(WRITE), .reset(RESET));  // open: Qn, preset
  D_Flip_Flop #(.trigger("falling")) d_ff_3 (
    .clk(C), .D(INPUT[2]), .Q(Q[2]), .en(WRITE), .reset(RESET));  // open: Qn, preset
  D_Flip_Flop #(.trigger("falling")) d_ff_4 (
    .clk(C), .D(INPUT[3]), .Q(Q[3]), .en(WRITE), .reset(RESET));  // open: Qn, preset
  D_Flip_Flop #(.trigger("falling")) d_ff_5 (
    .clk(C), .D(INPUT[4]), .Q(Q[4]), .en(WRITE), .reset(RESET));  // open: Qn, preset
  D_Flip_Flop #(.trigger("falling")) d_ff_6 (
    .clk(C), .D(INPUT[5]), .Q(Q[5]), .en(WRITE), .reset(RESET));  // open: Qn, preset
  D_Flip_Flop #(.trigger("falling")) d_ff_7 (
    .clk(C), .D(INPUT[6]), .Q(Q[6]), .en(WRITE), .reset(RESET));  // open: Qn, preset
  D_Flip_Flop #(.trigger("falling")) d_ff_8 (
    .clk(C), .D(INPUT[7]), .Q(Q[7]), .en(WRITE), .reset(RESET));  // open: Qn, preset
  D_Flip_Flop #(.trigger("falling")) d_ff_9 (
    .clk(C), .D(INPUT[8]), .Q(Q[8]), .en(WRITE), .reset(RESET));  // open: Qn, preset
  D_Flip_Flop #(.trigger("falling")) d_ff_10 (
    .clk(C), .D(INPUT[9]), .Q(Q[9]), .en(WRITE), .reset(RESET));  // open: Qn, preset
  D_Flip_Flop #(.trigger("falling")) d_ff_11 (
    .clk(C), .D(INPUT[10]), .Q(Q[10]), .en(WRITE), .reset(RESET));  // open: Qn, preset
  D_Flip_Flop #(.trigger("falling")) d_ff_12 (
    .clk(C), .D(INPUT[11]), .Q(Q[11]), .en(WRITE), .reset(RESET));  // open: Qn, preset
  D_Flip_Flop #(.trigger("falling")) d_ff_13 (
    .clk(C), .D(INPUT[12]), .Q(Q[12]), .en(WRITE), .reset(RESET));  // open: Qn, preset
  D_Flip_Flop #(.trigger("falling")) d_ff_14 (
    .clk(C), .D(INPUT[13]), .Q(Q[13]), .en(WRITE), .reset(RESET));  // open: Qn, preset
  D_Flip_Flop #(.trigger("falling")) d_ff_15 (
    .clk(C), .D(INPUT[14]), .Q(Q[14]), .en(WRITE), .reset(RESET));  // open: Qn, preset
  D_Flip_Flop #(.trigger("falling")) d_ff_16 (
    .clk(C), .D(INPUT[15]), .Q(Q[15]), .en(WRITE), .reset(RESET));  // open: Qn, preset
endmodule

module register_file (
  input  [15:0] DATA,
  input  [3:0] rd,
  input  WRITE,
  input  C,
  input  RESET,
  input  [3:0] rt,
  input  [3:0] rs,
  output [15:0] r0,
  output [15:0] r1,
  output [15:0] r2,
  output [15:0] r3,
  output [15:0] r4,
  output [15:0] r5,
  output [15:0] r6,
  output [15:0] r7,
  output [15:0] r8,
  output [15:0] r9,
  output [15:0] r10,
  output [15:0] r11,
  output [15:0] r12,
  output [15:0] r13,
  output [15:0] r14,
  output [15:0] r15,
  output [15:0] T,
  output [15:0] S
);

  wire and_1_out, and_2_out, and_3_out, and_4_out, and_5_out, and_6_out, and_7_out, and_8_out, and_9_out,
       and_10_out, and_11_out, and_12_out, and_13_out, and_14_out, and_15_out, and_16_out, decoder_1_out0,
       decoder_1_out1, decoder_1_out2, decoder_1_out3, decoder_1_out4, decoder_1_out5, decoder_1_out6,
       decoder_1_out7, decoder_1_out8, decoder_1_out9, decoder_1_out10, decoder_1_out11, decoder_1_out12,
       decoder_1_out13, decoder_1_out14, decoder_1_out15;

  Decoder #(.select(4), .enable("false")) decoder_1 (
    .out0(decoder_1_out0), .out1(decoder_1_out1), .out2(decoder_1_out2), .out3(decoder_1_out3),
    .out4(decoder_1_out4), .out5(decoder_1_out5), .out6(decoder_1_out6), .out7(decoder_1_out7),
    .out8(decoder_1_out8), .out9(decoder_1_out9), .out10(decoder_1_out10), .out11(decoder_1_out11),
    .out12(decoder_1_out12), .out13(decoder_1_out13), .out14(decoder_1_out14), .out15(decoder_1_out15),
    .sel(rd));
  and and_1 (and_1_out, WRITE, decoder_1_out0);
  and and_2 (and_2_out, WRITE, decoder_1_out1);
  and and_3 (and_3_out, WRITE, decoder_1_out2);
  and and_4 (and_4_out, WRITE, decoder_1_out3);
  and and_5 (and_5_out, WRITE, decoder_1_out4);
  and and_6 (and_6_out, WRITE, decoder_1_out5);
  and and_7 (and_7_out, WRITE, decoder_1_out6);
  and and_8 (and_8_out, WRITE, decoder_1_out7);
  and and_9 (and_9_out, WRITE, decoder_1_out8);
  and and_10 (and_10_out, WRITE, decoder_1_out9);
  and and_11 (and_11_out, WRITE, decoder_1_out10);
  and and_12 (and_12_out, WRITE, decoder_1_out11);
  and and_13 (and_13_out, WRITE, decoder_1_out12);
  and and_14 (and_14_out, WRITE, decoder_1_out13);
  and and_15 (and_15_out, WRITE, decoder_1_out14);
  and and_16 (and_16_out, WRITE, decoder_1_out15);
  _16_bit_register u_16_bit_register_1 (.C(C), .INPUT({16{1'b0}}), .Q(r0), .RESET(RESET), .WRITE(and_1_out));
  _16_bit_register u_16_bit_register_2 (.C(C), .INPUT(DATA), .Q(r1), .RESET(RESET), .WRITE(and_2_out));
  _16_bit_register u_16_bit_register_3 (.C(C), .INPUT(DATA), .Q(r2), .RESET(RESET), .WRITE(and_3_out));
  _16_bit_register u_16_bit_register_4 (.C(C), .INPUT(DATA), .Q(r3), .RESET(RESET), .WRITE(and_4_out));
  _16_bit_register u_16_bit_register_5 (.C(C), .INPUT(DATA), .Q(r4), .RESET(RESET), .WRITE(and_5_out));
  _16_bit_register u_16_bit_register_6 (.C(C), .INPUT(DATA), .Q(r5), .RESET(RESET), .WRITE(and_6_out));
  _16_bit_register u_16_bit_register_7 (.C(C), .INPUT(DATA), .Q(r6), .RESET(RESET), .WRITE(and_7_out));
  _16_bit_register u_16_bit_register_8 (.C(C), .INPUT(DATA), .Q(r7), .RESET(RESET), .WRITE(and_8_out));
  _16_bit_register u_16_bit_register_9 (.C(C), .INPUT(DATA), .Q(r8), .RESET(RESET), .WRITE(and_9_out));
  _16_bit_register u_16_bit_register_10 (.C(C), .INPUT(DATA), .Q(r9), .RESET(RESET), .WRITE(and_10_out));
  _16_bit_register u_16_bit_register_11 (.C(C), .INPUT(DATA), .Q(r10), .RESET(RESET), .WRITE(and_11_out));
  _16_bit_register u_16_bit_register_12 (.C(C), .INPUT(DATA), .Q(r11), .RESET(RESET), .WRITE(and_12_out));
  _16_bit_register u_16_bit_register_13 (.C(C), .INPUT(DATA), .Q(r12), .RESET(RESET), .WRITE(and_13_out));
  _16_bit_register u_16_bit_register_14 (.C(C), .INPUT(DATA), .Q(r13), .RESET(RESET), .WRITE(and_14_out));
  _16_bit_register u_16_bit_register_15 (.C(C), .INPUT(DATA), .Q(r14), .RESET(RESET), .WRITE(and_15_out));
  _16_bit_register u_16_bit_register_16 (.C(C), .INPUT(DATA), .Q(r15), .RESET(RESET), .WRITE(and_16_out));
  Multiplexer #(.select(4), .width(16), .enable("false")) multiplexer_1 (
    .in0(r0), .in1(r1), .in2(r2), .in3(r3), .in4(r4), .in5(r5), .in6(r6), .in7(r7), .in8(r8), .in9(r9),
    .in10(r10), .in11(r11), .in12(r12), .in13(r13), .in14(r14), .in15(r15), .out(T), .sel(rt));
  Multiplexer #(.select(4), .width(16), .enable("false")) multiplexer_2 (
    .in0(r0), .in1(r1), .in2(r2), .in3(r3), .in4(r4), .in5(r5), .in6(r6), .in7(r7), .in8(r8), .in9(r9),
    .in10(r10), .in11(r11), .in12(r12), .in13(r13), .in14(r14), .in15(r15), .out(S), .sel(rs));

  // Notes on the sheet:
  //   r1 ALWAYS ZERO
  //   register rt content
  //   register rs content
endmodule

module control_unit (
  input  [3:0] rt,
  input  [3:0] OP_CODE,
  output [3:0] rt_2,
  output MemToReg,
  output MemRead,
  output MemWrite,
  output ALUSrc,
  output RegWrite,
  output RegDst,
  output [3:0] ALU_CODE
);

  wire ADD_out, AND_out, CP_out, EQ_out, GT_out, INV_out, LT_out, NEQ_out, NOT_2_out, OR_out, R_TYPE_out,
       SLA_out, SLL_out, SRA_out, SRL_out, SUB_out, ZERO_out;

  and ZERO (ZERO_out, ~OP_CODE[0], ~OP_CODE[1], ~OP_CODE[2], ~OP_CODE[3]);  // AND_Gate
  and R_TYPE (R_TYPE_out, OP_CODE[0], ~OP_CODE[1], ~OP_CODE[2], ~OP_CODE[3]);  // AND_Gate
  and AND (AND_out, ~OP_CODE[0], OP_CODE[1], ~OP_CODE[2], ~OP_CODE[3]);  // AND_Gate
  and OR (OR_out, OP_CODE[0], OP_CODE[1], ~OP_CODE[2], ~OP_CODE[3]);  // AND_Gate
  or or_2 (ALU_CODE[0], OR_out, SUB_out, GT_out, NEQ_out, NOT_2_out, SLL_out, SLA_out, CP_out);
  and ADD (ADD_out, ~OP_CODE[0], ~OP_CODE[1], OP_CODE[2], ~OP_CODE[3]);  // AND_Gate
  and SUB (SUB_out, OP_CODE[0], ~OP_CODE[1], OP_CODE[2], ~OP_CODE[3]);  // AND_Gate
  and LT (LT_out, ~OP_CODE[0], OP_CODE[1], OP_CODE[2], ~OP_CODE[3]);  // AND_Gate
  and GT (GT_out, OP_CODE[0], OP_CODE[1], OP_CODE[2], ~OP_CODE[3]);  // AND_Gate
  and EQ (EQ_out, ~OP_CODE[0], ~OP_CODE[1], ~OP_CODE[2], OP_CODE[3]);  // AND_Gate
  or or_3 (ALU_CODE[1], OR_out, LT_out, GT_out, AND_out, CP_out, INV_out, SLL_out, SRA_out);
  and NEQ (NEQ_out, OP_CODE[0], ~OP_CODE[1], ~OP_CODE[2], OP_CODE[3]);  // AND_Gate
  and LW (MemRead, ~OP_CODE[0], OP_CODE[1], ~OP_CODE[2], OP_CODE[3]);  // AND_Gate
  LED led_1 (.in(OP_CODE[0]));
  LED led_2 (.in(OP_CODE[1]));
  LED led_3 (.in(OP_CODE[2]));
  LED led_4 (.in(OP_CODE[3]));
  and SW (MemWrite, OP_CODE[0], OP_CODE[1], ~OP_CODE[2], OP_CODE[3]);  // AND_Gate
  not not_1 (RegWrite, MemWrite);
  or or_4 (ALU_CODE[2], ADD_out, SUB_out, LT_out, GT_out, MemWrite, MemRead, SRL_out, SLA_out, SRA_out, CP_out);
  // AND_Gate ZERO_2 has open pins: in0=rt[0], in1=rt[1], in2=rt[2], in3=rt[3], in4=ZERO_out, out=open
  and NOT_2 (NOT_2_out, rt[0], ~rt[1], ~rt[2], ~rt[3], R_TYPE_out);  // AND_Gate
  and INV (INV_out, ~rt[0], rt[1], ~rt[2], rt[3], R_TYPE_out);  // AND_Gate
  or or_5 (ALUSrc, MemWrite, MemRead);
  and SLL (SLL_out, rt[0], rt[1], ~rt[2], rt[3], R_TYPE_out);  // AND_Gate
  and SRL (SRL_out, ~rt[0], ~rt[1], rt[2], rt[3], R_TYPE_out);  // AND_Gate
  or or_6 (ALU_CODE[3], EQ_out, NEQ_out, CP_out, INV_out, SLL_out, SRL_out, SLA_out, SRA_out);
  and SLA (SLA_out, rt[0], ~rt[1], rt[3], rt[3], R_TYPE_out);  // AND_Gate
  and SRA (SRA_out, ~rt[0], rt[1], rt[2], rt[3], R_TYPE_out);  // AND_Gate
  LED led_5 (.in(R_TYPE_out));
  LED led_6 (.in(rt[0]));
  LED led_7 (.in(rt[1]));
  LED led_8 (.in(rt[2]));
  LED led_9 (.in(rt[3]));
  and CP (CP_out, rt[0], rt[1], rt[2], rt[3], R_TYPE_out);

  assign MemToReg = MemRead;
  assign RegDst = MemWrite;
  assign rt_2 = rt;

  // Notes on the sheet:
  //   bits  12 - 15
  //   zero
  //   bits 0 - 3
  //   register operations, function depends on 0 - 3 bits
endmodule

module warehouse_robo (
  input  [2:0] source,
  input  start,
  input  [2:0] target,
  input  front,
  input  reset,
  input  left,
  input  right,
  input  desitnation,
  output LEFT_MOTOR_OUT_,
  output RIGHT_MOTOR_OUT
);

  wire and_1_out, and_2_out, and_3_out, and_4_out, blocked_out, not_1_out, not_2_out, not_3_out, not_4_out,
       not_5_out, or_1_out, or_2_out, or_3_out, undriven, undriven_2;

  not not_1 (not_1_out, reset);
  and and_1 (and_1_out, start, not_1_out);
  LED led_1 (.in(and_1_out));
  LED led_2 (.in(front));
  LED led_3 (.in(left));
  LED led_4 (.in(right));
  LED led_5 (.in(desitnation));
  not not_2 (not_2_out, front);
  not not_3 (not_3_out, left);
  not not_4 (not_4_out, right);
  not not_5 (not_5_out, desitnation);
  and and_2 (and_2_out, not_3_out, not_2_out, not_5_out, not_4_out);
  and blocked (blocked_out, front, left, right);
  LED forward (.in(and_2_out));
  and and_3 (and_3_out, not_2_out, left, not_4_out, not_5_out);
  and and_4 (and_4_out, not_2_out, not_3_out, not_5_out);
  LED turnleft (.in(and_4_out));
  or or_1 (or_1_out, blocked_out, desitnation);
  LED turnright (.in(and_3_out));
  LED stop (.in(or_1_out));
  or or_2 (or_2_out, and_2_out, and_3_out);
  or or_3 (or_3_out, and_2_out, and_4_out);
  and and_5 (LEFT_MOTOR_OUT_, or_2_out, and_1_out);
  and and_6 (RIGHT_MOTOR_OUT, or_3_out, and_1_out);
  LED leftmotor (.in(LEFT_MOTOR_OUT_));
  LED rightmotore (.in(RIGHT_MOTOR_OUT));
  LED LEFT_DIR (.in(undriven));
  LED RIGHT_DIR (.in(undriven_2));
endmodule

module warehouse_sys (
  input  start,
  input  front,
  input  left,
  input  right,
  input  CPU_MODE,
  input  destination,
  input  resest,
  input  [2:0] x1,
  input  [2:0] y1
);

  wire and_25_out, clock_1_out, collect1_q, comparator_1_eq, comparator_2_eq, comparator_3_eq,
       comparator_4_eq, comparator_5_eq, comparator_6_eq, decoder_3_out1, decoder_4_out0, decoder_4_out1,
       decoder_4_out2, decoder_4_out3, decoder_5_out0, decoder_5_out1, decoder_5_out2, decoder_5_out3,
       decoder_6_out0, decoder_6_out1, decoder_6_out2, decoder_6_out3, decoder_6_out4, decoder_6_out5,
       decoder_6_out6, decoder_6_out7, down_move_out, down_valid_out, left_move_out, multiplexer_4_out,
       multiplexer_5_out, not_1_out, not_2_out, not_3_out, not_4_out, or_1_out, or_2_out, or_13_out,
       pickup1_at_location_out, pickup_visible_out, right_move_out, right_valid_out, up_move_out,
       warehouse_robo_1_left_motor_out_, warehouse_robo_1_right_motor_out;
  wire [1:0] adder_1_out, adder_2_out, direction_q, left_valid_out, main_1_r2_2, multiplexer_3_out,
       up_valid_out;
  wire [2:0] adder_3_out, adder_4_out, adder_5_out, adder_6_out, multiplexer_1_out, multiplexer_2_out, x_q,
       y_q;
  wire [7:0] and_1_out, and_2_out, and_3_out, and_4_out, and_5_out, and_6_out, and_7_out, and_8_out,
       and_17_out, and_18_out, and_19_out, and_20_out, and_21_out, and_22_out, and_23_out, and_24_out,
       decoder_1_out7, decoder_7_out7, or_4_out, or_5_out, or_6_out, or_7_out, or_8_out, or_9_out, or_10_out,
       or_11_out;
  wire [7:7] and_9_out, and_10_out, and_11_out, and_12_out, and_13_out, and_14_out, and_15_out, and_16_out,
       decoder_2_out0, decoder_2_out1, decoder_2_out2, decoder_2_out3, decoder_2_out4, decoder_2_out5,
       decoder_2_out6, decoder_2_out7;
  wire [13:0] main_1_r2;

  Decoder #(.select(3)) decoder_1 (
    .out0(decoder_1_out7[7]), .out1(decoder_1_out7[6]), .out2(decoder_1_out7[5]), .out3(decoder_1_out7[4]),
    .out4(decoder_1_out7[3]), .out5(decoder_1_out7[2]), .out6(decoder_1_out7[1]), .out7(decoder_1_out7[0]),
    .sel(x_q), .en(1'b1));
  main main_1 (.r2({main_1_r2_2, main_1_r2}));  // open: pc, r0, r1, r3, r4, r5, r6, r7, r8, r9, r10, r11, r12, r13, r14, r15, halt
  Decoder #(.select(3)) decoder_2 (
    .out0(decoder_2_out0[7]), .out1(decoder_2_out1[7]), .out2(decoder_2_out2[7]), .out3(decoder_2_out3[7]),
    .out4(decoder_2_out4[7]), .out5(decoder_2_out5[7]), .out6(decoder_2_out6[7]), .out7(decoder_2_out7[7]),
    .sel(y_q), .en(1'b1));
  warehouse_robo warehouse_robo_1 (
    .start(start), .front(front), .reset(resest), .left(left), .right(right), .desitnation(destination),
    .LEFT_MOTOR_OUT_(warehouse_robo_1_left_motor_out_), .RIGHT_MOTOR_OUT(warehouse_robo_1_right_motor_out));  // open: source, target
  Decoder #(.select(2)) decoder_3 (.out1(decoder_3_out1), .sel(main_1_r2[1:0]), .en(1'b1));  // open: out0, out2, out3
  Register #(.width(3)) x (.D(multiplexer_1_out), .en(1'b1), .Q(x_q), .clk(clock_1_out));  // open: clr
  Register #(.width(3)) y (.D(multiplexer_2_out), .en(1'b1), .Q(y_q), .clk(clock_1_out));  // open: clr
  Register #(.width(2)) direction (.D(multiplexer_3_out), .en(1'b1), .Q(direction_q), .clk(clock_1_out));  // open: clr
  assign and_1_out = decoder_1_out7 & {8{decoder_2_out0[7]}};  // AND_Gate and_1, 8 bits wide
  assign and_2_out = decoder_1_out7 & {8{decoder_2_out1[7]}};  // AND_Gate and_2, 8 bits wide
  assign and_3_out = decoder_1_out7 & {8{decoder_2_out2[7]}};  // AND_Gate and_3, 8 bits wide
  assign and_4_out = decoder_1_out7 & {8{decoder_2_out3[7]}};  // AND_Gate and_4, 8 bits wide
  assign and_5_out = decoder_1_out7 & {8{decoder_2_out4[7]}};  // AND_Gate and_5, 8 bits wide
  assign and_6_out = decoder_1_out7 & {8{decoder_2_out5[7]}};  // AND_Gate and_6, 8 bits wide
  assign and_7_out = decoder_1_out7 & {8{decoder_2_out6[7]}};  // AND_Gate and_7, 8 bits wide
  assign and_8_out = decoder_1_out7 & {8{decoder_2_out7[7]}};  // AND_Gate and_8, 8 bits wide
  Decoder #(.select(2)) decoder_4 (
    .out0(decoder_4_out0), .out1(decoder_4_out1), .out2(decoder_4_out2), .out3(decoder_4_out3),
    .sel(main_1_r2[1:0]), .en(1'b1));
  Adder #(.width(2)) adder_1 (.a(direction_q), .b(2'b11), .out(adder_1_out), .cin(1'b0));  // open: cout
  Adder #(.width(2)) adder_2 (.a(direction_q), .b(2'b01), .out(adder_2_out), .cin(1'b0));  // open: cout
  LED led_1 (.in(decoder_4_out0));
  LED led_2 (.in(decoder_4_out2));
  Adder #(.width(3)) adder_3 (.a(x_q), .b(3'b001), .out(adder_3_out), .cin(1'b0));  // open: cout
  Adder #(.width(3)) adder_4 (.a(y_q), .b(3'b001), .out(adder_4_out), .cin(1'b0));  // open: cout
  Adder #(.width(3)) adder_5 (.a(y_q), .b(3'b111), .out(adder_5_out), .cin(1'b0));  // open: cout
  or or_1 (or_1_out, decoder_4_out1, decoder_4_out2);
  Multiplexer #(.select(2), .width(3)) multiplexer_1 (
    .in0(x_q), .in1(x_q), .in2(adder_3_out), .in3(adder_6_out), .out(multiplexer_1_out),
    .sel(left_valid_out), .en(1'b1));
  Multiplexer #(.select(2), .width(3)) multiplexer_2 (
    .in0(y_q), .in1(y_q), .in2(adder_4_out), .in3(adder_5_out), .out(multiplexer_2_out), .sel(up_valid_out),
    .en(1'b1));
  Multiplexer #(.select(2), .width(2)) multiplexer_3 (
    .in0(direction_q), .in1(direction_q), .in2(adder_1_out), .in3(adder_2_out), .out(multiplexer_3_out),
    .sel(main_1_r2[1:0]), .en(1'b1));
  or or_2 (or_2_out, decoder_4_out1, decoder_4_out3);
  Multiplexer #(.enable("false")) multiplexer_4 (
    .in0(warehouse_robo_1_left_motor_out_), .in1(or_2_out), .out(multiplexer_4_out), .sel(CPU_MODE));
  Decoder #(.select(2)) decoder_5 (
    .out0(decoder_5_out0), .out1(decoder_5_out1), .out2(decoder_5_out2), .out3(decoder_5_out3),
    .sel(direction_q), .en(1'b1));
  LED led_3 (.in(multiplexer_4_out));
  Multiplexer #(.enable("false")) multiplexer_5 (
    .in0(warehouse_robo_1_right_motor_out), .in1(or_1_out), .out(multiplexer_5_out), .sel(CPU_MODE));
  LED led_4 (.in(multiplexer_5_out));
  Adder #(.width(3)) adder_6 (.a(x_q), .b(3'b111), .out(adder_6_out), .cin(1'b0));  // open: cout
  and right_move (right_move_out, decoder_3_out1, decoder_5_out1);
  and up_move (up_move_out, decoder_3_out1, decoder_5_out0);
  Clock clock_1 (.out(clock_1_out));
  and left_move (left_move_out, decoder_3_out1, decoder_5_out3);
  or or_3 (up_valid_out[1], down_valid_out, up_valid_out[0]);
  and down_move (down_move_out, decoder_3_out1, decoder_5_out2);
  assign or_4_out = and_1_out | and_17_out;  // OR_Gate or_4, 8 bits wide
  assign or_5_out = and_2_out | and_18_out;  // OR_Gate or_5, 8 bits wide
  assign or_6_out = and_3_out | and_19_out;  // OR_Gate or_6, 8 bits wide
  assign or_7_out = and_4_out | and_20_out;  // OR_Gate or_7, 8 bits wide
  assign or_8_out = and_5_out | and_21_out;  // OR_Gate or_8, 8 bits wide
  assign or_9_out = and_6_out | and_22_out;  // OR_Gate or_9, 8 bits wide
  assign or_10_out = and_7_out | and_23_out;  // OR_Gate or_10, 8 bits wide
  assign or_11_out = and_8_out | and_24_out;  // OR_Gate or_11, 8 bits wide
  Comparator #(.width(3)) comparator_1 (.a(y_q), .b(3'b111), .eq(comparator_1_eq));  // open: gt, lt
  Comparator #(.width(3)) comparator_2 (.a(x_q), .b(3'b111), .eq(comparator_2_eq));  // open: gt, lt
  or or_12 (left_valid_out[1], right_valid_out, left_valid_out[0]);
  Decoder #(.select(3)) decoder_6 (
    .out0(decoder_6_out0), .out1(decoder_6_out1), .out2(decoder_6_out2), .out3(decoder_6_out3),
    .out4(decoder_6_out4), .out5(decoder_6_out5), .out6(decoder_6_out6), .out7(decoder_6_out7), .sel(y1),
    .en(1'b1));
  DotMatrix #(.inputtype("row"), .matrixcols(8), .matrixrows(8)) dotmatrix_1 (
    .row0(or_4_out), .row1(or_5_out), .row2(or_6_out), .row3(or_7_out), .row4(or_8_out), .row5(or_9_out),
    .row6(or_10_out), .row7(or_11_out));
  not not_1 (not_1_out, comparator_1_eq);
  not not_2 (not_2_out, comparator_2_eq);
  and down_valid (down_valid_out, not_1_out, down_move_out);
  and right_valid (right_valid_out, not_2_out, right_move_out);
  Comparator #(.width(3)) comparator_3 (.a(x_q), .b(3'b000), .eq(comparator_3_eq));  // open: gt, lt
  and and_9 (and_9_out[7], decoder_6_out0, and_25_out);
  and and_10 (and_10_out[7], decoder_6_out1, and_25_out);
  and and_11 (and_11_out[7], decoder_6_out2, and_25_out);
  and and_12 (and_12_out[7], decoder_6_out3, and_25_out);
  and and_13 (and_13_out[7], decoder_6_out4, and_25_out);
  and and_14 (and_14_out[7], decoder_6_out5, and_25_out);
  and and_15 (and_15_out[7], decoder_6_out6, and_25_out);
  and and_16 (and_16_out[7], decoder_6_out7, and_25_out);
  Comparator #(.width(3)) comparator_4 (.a(y_q), .b(3'b000), .eq(comparator_4_eq));  // open: gt, lt
  not not_3 (not_3_out, comparator_4_eq);
  not not_4 (not_4_out, comparator_3_eq);
  and up_valid (up_valid_out[0], not_3_out, up_move_out);
  and left_valid (left_valid_out[0], not_4_out, left_move_out);
  Decoder #(.select(3)) decoder_7 (
    .out0(decoder_7_out7[7]), .out1(decoder_7_out7[6]), .out2(decoder_7_out7[5]), .out3(decoder_7_out7[4]),
    .out4(decoder_7_out7[3]), .out5(decoder_7_out7[2]), .out6(decoder_7_out7[1]), .out7(decoder_7_out7[0]),
    .sel(x1), .en(1'b1));
  Comparator #(.width(3)) comparator_5 (.a(x_q), .b(x1), .eq(comparator_5_eq));  // open: gt, lt
  Comparator #(.width(3)) comparator_6 (.a(y_q), .b(y1), .eq(comparator_6_eq));  // open: gt, lt
  and pickup1_at_location (pickup1_at_location_out, comparator_5_eq, comparator_6_eq);
  Register #(.width(1)) collect1 (.D(or_13_out), .Q(collect1_q), .clk(clock_1_out));  // open: en, clr
  assign and_17_out = decoder_7_out7 & {8{and_9_out[7]}};  // AND_Gate and_17, 8 bits wide
  assign and_18_out = decoder_7_out7 & {8{and_10_out[7]}};  // AND_Gate and_18, 8 bits wide
  assign and_19_out = decoder_7_out7 & {8{and_11_out[7]}};  // AND_Gate and_19, 8 bits wide
  assign and_20_out = decoder_7_out7 & {8{and_12_out[7]}};  // AND_Gate and_20, 8 bits wide
  assign and_21_out = decoder_7_out7 & {8{and_13_out[7]}};  // AND_Gate and_21, 8 bits wide
  assign and_22_out = decoder_7_out7 & {8{and_14_out[7]}};  // AND_Gate and_22, 8 bits wide
  assign and_23_out = decoder_7_out7 & {8{and_15_out[7]}};  // AND_Gate and_23, 8 bits wide
  assign and_24_out = decoder_7_out7 & {8{and_16_out[7]}};  // AND_Gate and_24, 8 bits wide
  not pickup_visible (pickup_visible_out, collect1_q);
  buf and_25 (and_25_out, pickup_visible_out);  // AND_Gate
  or or_13 (or_13_out, collect1_q, pickup1_at_location_out);

  // Notes on the sheet:
  //   left motor
endmodule
